// Digital circuit 2023CPU16.dig as structural Verilog
module _2023CPU16 (
  input  [15:0] ROM_INSTR,
  input  [15:0] ROM_IMM,
  input  CLK_CPU,
  input  [15:0] PINA,
  input  [15:0] PINB,
  input  [15:0] TRX,
  output [15:0] ROM_ADDR,
  output [15:0] ROM_IMM_ADDR,
  output [15:0] PORTA,
  output [15:0] PORTB,
  output [15:0] TTX,
  output [15:0] PULSE
);

  wire and_1_out, and_3_out, and_4_out, and_7_out, and_8_out, and_9_out, and_10_out, and_11_out, and_12_out,
       and_13_out, and_14_out, and_15_out, and_16_out, and_17_out, and_18_out, bitselector_1_out,
       comparator_1_eq, comparator_2_lt, comparator_3_lt, comparator_4_eq, counter_1_ovf, decoder_1_out_3,
       decoder_3_out_0, decoder_3_out_1, ELPM_9__11, ELPM_en, F_C, F_N, F_V, F_Z, INT, INT_PINA,
       INTERRUPT_MGR_any, IS_RW_out, IS_STACK_out, lookuptable_1_out, MODE_ALU, MODE_BRANCH, MODE_MEM,
       multiplexer_7_out, multiplexer_8_out, not_1_out, not_2_out, not_3_out, not_4_out, not_5_out,
       not_6_out, not_7_out, or_1_out, or_2_out, or_3_out, or_4_out, PHASE_0, PHASE_1, PHASE_2, xnor_1_out,
       zero_1_iszero;
  wire [1:0] ADDRBUS_SEL_out, counter_1_out;
  wire [3:0] alu_1_r_n, INT_NXT;
  wire [7:4] FLAGS;
  wire [15:0] add_1_s, add_2_s, add_3_s, alu_1_r, and_2_out, GIMSK, GPR_A, GPR_B, IMM, INSTR,
       iomem_1_gram_flip, iomem_1_reader, iomem_1_rvalue, iomem_1_sp, iomem_1_writer, multiplexer_1_out,
       multiplexer_2_out, multiplexer_3_out, multiplexer_4_out, multiplexer_6_out, multiplexer_9_out,
       multiplexer_10_out, multiplexer_11_out, multiplexer_12_out, multiplexer_13_out, multiplexer_14_out,
       PINA_BUF_q, PINB_BUF_q, ramdualport_1_d, sub_1_s, TRX_BUF_q, xor_1_out;
  wire [15:8] iomem_1_flags;

  BitSelector #(.Selector_Bits(3)) bitselector_1 (
    .in({FLAGS, F_V, F_N, F_Z, F_C}), .sel(INSTR[6:4]), .out(bitselector_1_out));
  xnor xnor_1 (xnor_1_out, bitselector_1_out, INSTR[7]);
  or or_1 (or_1_out, ~INSTR[8], xnor_1_out);  // Or
  PullDown #(.Bits(16)) pulldown_1 (.out(TRX));
  PullDown #(.Bits(16)) pulldown_2 (.out(PINA));
  and and_1 (and_1_out, MODE_BRANCH, or_1_out);
  PullDown #(.Bits(16)) pulldown_3 (.out(PINB));
  Counter #(.Bits(2)) counter_1 (.en(1'b1), .C(CLK_CPU), .clr(PHASE_2), .out(counter_1_out), .ovf(counter_1_ovf));
  assign and_2_out = {{15{1'b0}}, INT_PINA} & GIMSK;  // And and_2, 16 bits wide
  Decoder #(.Selector_Bits(2)) decoder_1 (
    .sel(counter_1_out), .out_0(PHASE_0), .out_1(PHASE_1), .out_2(PHASE_2), .out_3(decoder_1_out_3));
  Register #(.Bits(16)) u_INSTR (.D(ROM_INSTR), .C(CLK_CPU), .en(or_2_out), .Q(INSTR));
  Register #(.Bits(16)) u_IMM (.D(ROM_IMM), .C(CLK_CPU), .en(or_2_out), .Q(IMM));
  Comparator #(.Bits(4)) comparator_1 (.a(INSTR[12:9]), .b(4'b0000), .eq(comparator_1_eq));  // open: gt, lt
  Multiplexer #(.Bits(16)) multiplexer_1 (
    .sel(and_1_out), .in_0(add_1_s), .in_1(multiplexer_2_out), .out(multiplexer_1_out));
  or or_2 (or_2_out, ELPM_en, PHASE_0);
  and and_3 (and_3_out, comparator_1_eq, MODE_BRANCH);
  Multiplexer #(.Bits(16)) multiplexer_2 (.sel(and_3_out), .in_0(GPR_A), .in_1(IMM), .out(multiplexer_2_out));
  Multiplexer #(.Bits(16)) multiplexer_3 (.sel(INT), .in_0(multiplexer_1_out), .in_1(16'h2), .out(multiplexer_3_out));
  Break break_1 (.brk(PHASE_0));
  Register #(.Bits(16)) IP (.D(multiplexer_3_out), .C(CLK_CPU), .en(PHASE_2), .Q(ROM_ADDR));
  or or_3 (or_3_out, and_3_out, and_4_out, and_18_out);
  and and_4 (and_4_out, INSTR[12], MODE_MEM);
  PriorityEncoder #(.Selector_Bits(4)) INTERRUPT_MGR (
    .in0(and_2_out[0]), .in1(and_2_out[1]), .in2(and_2_out[2]), .in3(and_2_out[3]), .in4(and_2_out[4]),
    .in5(and_2_out[5]), .in6(and_2_out[6]), .in7(and_2_out[7]), .in8(and_2_out[8]), .in9(and_2_out[9]),
    .in10(and_2_out[10]), .in11(and_2_out[11]), .in12(and_2_out[12]), .in13(and_2_out[13]),
    .in14(and_2_out[14]), .in15(and_2_out[15]), .num(INT_NXT), .any(INTERRUPT_MGR_any));
  LookUpTable lookuptable_1 (.in0(MODE_ALU), .in1(MODE_MEM), .out(lookuptable_1_out));
  Multiplexer #(.Bits(16)) multiplexer_4 (.sel(or_3_out), .in_0({16{1'b0}}), .in_1(16'h1), .out(multiplexer_4_out));
  Add #(.Bits(16)) add_1 (.a(ROM_ADDR), .b(multiplexer_4_out), .c_i(1'b1), .s(add_1_s));  // open: c_o
  Add #(.Bits(16)) add_2 (.a(ROM_ADDR), .b({16{1'b0}}), .c_i(1'b1), .s(add_2_s));  // open: c_o
  Decoder #(.Selector_Bits(2)) decoder_2 (
    .sel(INSTR[15:14]), .out_0(MODE_ALU), .out_1(MODE_MEM), .out_2(MODE_BRANCH));  // open: out_3
  Multiplexer #(.Bits(16)) multiplexer_5 (.sel(ELPM_en), .in_0(add_2_s), .in_1(GPR_B), .out(ROM_IMM_ADDR));
  and and_5 (ELPM_en, MODE_MEM, ELPM_9__11);
  and and_6 (INT, INTERRUPT_MGR_any, FLAGS[7]);
  and and_7 (and_7_out, PHASE_2, not_1_out);
  not not_1 (not_1_out, INSTR[8]);
  Multiplexer #(.Bits(16)) multiplexer_6 (
    .sel(lookuptable_1_out), .in_0(alu_1_r), .in_1(multiplexer_13_out), .out(multiplexer_6_out));
  Multiplexer multiplexer_7 (.sel(lookuptable_1_out), .in_0(PHASE_2), .in_1(and_7_out), .out(multiplexer_7_out));
  Multiplexer multiplexer_8 (.sel(not_2_out), .in_0(PHASE_2), .in_1(PHASE_1), .out(multiplexer_8_out));
  and and_8 (and_8_out, multiplexer_7_out, ~MODE_BRANCH);  // And
  LookUpTable IS_STACK (.in0(ADDRBUS_SEL_out[0]), .in1(ADDRBUS_SEL_out[1]), .out(IS_STACK_out));
  and and_9 (and_9_out, MODE_ALU, PHASE_2);
  and and_10 (and_10_out, multiplexer_8_out, MODE_MEM, IS_STACK_out);
  not not_2 (not_2_out, and_14_out);
  LookUpTable IS_RW (.in0(INSTR[9]), .in1(INSTR[10]), .in2(INSTR[11]), .out(IS_RW_out));
  RegisterFile #(.AddrBits(4), .Bits(16)) GPRs (
    .Din(multiplexer_6_out), .we(and_8_out), .Rw(INSTR[3:0]), .C(CLK_CPU), .Ra(INSTR[3:0]), .Rb(INSTR[7:4]),
    .Da(GPR_A), .Db(GPR_B));
  Decoder decoder_3 (.sel(INSTR[8]), .out_0(decoder_3_out_0), .out_1(decoder_3_out_1));
  and and_11 (and_11_out, IS_RW_out, PHASE_2, MODE_MEM);
  Register #(.Bits(16)) TRX_BUF (.D(TRX), .C(PHASE_2), .en(PHASE_2), .Q(TRX_BUF_q));
  Multiplexer #(.Selector_Bits(2), .Bits(16)) multiplexer_9 (
    .sel(ADDRBUS_SEL_out), .in_0(multiplexer_10_out), .in_1(iomem_1_sp), .in_2(multiplexer_14_out),
    .in_3({16{1'b0}}), .out(multiplexer_9_out));
  and and_12 (and_12_out, and_11_out, decoder_3_out_0);
  and and_13 (and_13_out, decoder_3_out_1, and_11_out);
  Multiplexer #(.Bits(16)) multiplexer_10 (.sel(not_3_out), .in_0(IMM), .in_1(GPR_B), .out(multiplexer_10_out));
  and and_14 (and_14_out, MODE_MEM, INSTR[8]);
  Register #(.Bits(16)) PINB_BUF (.D(PINB), .C(PHASE_2), .en(PHASE_2), .Q(PINB_BUF_q));
  ALU alu_1 (
    .A(GPR_A), .B(GPR_B), .OP(INSTR[13:9]), .C_en(INSTR[8]), .C_in(F_C), .R(alu_1_r), .R_N(alu_1_r_n[2]),
    .R_C(alu_1_r_n[0]), .R_V(alu_1_r_n[3]), .R_Z(alu_1_r_n[1]));
  Comparator #(.Bits(16)) comparator_2 (.a(multiplexer_9_out), .b(16'h20), .lt(comparator_2_lt));  // open: gt, eq
  not not_3 (not_3_out, INSTR[12]);
  LookUpTable #(.Bits(2)) ADDRBUS_SEL (.in0(INSTR[9]), .in1(INSTR[10]), .in2(INSTR[11]), .out(ADDRBUS_SEL_out));
  not not_4 (not_4_out, comparator_2_lt);
  and and_15 (and_15_out, not_4_out, and_14_out);
  not not_5 (not_5_out, and_15_out);
  Register #(.Bits(16)) PINA_BUF (.D(PINA), .C(PHASE_2), .en(PHASE_2), .Q(PINA_BUF_q));
  and and_16 (and_16_out, and_14_out, comparator_2_lt);
  IOMEM iomem_1 (
    .WADDR(multiplexer_9_out[4:0]), .WVALUE(GPR_A), .FLAGSIN({{8{1'b0}}, FLAGS, alu_1_r_n}),
    .W_EN(and_16_out), .FLAGSW_EN(and_9_out), .CLK(CLK_CPU), .RADDR(multiplexer_9_out[4:0]),
    .SPW_EN(and_10_out), .SPIN(add_3_s), .PINA(PINA_BUF_q), .PINB(PINB_BUF_q), .TRX(TRX_BUF_q),
    .INTNO({{12{1'b0}}, INT_NXT}), .IRETA(add_1_s), .INT_EN(INT), .READER_ACTIVE(and_12_out),
    .WRITER_ACTIVE(and_13_out), .SP(iomem_1_sp), .FLAGS({iomem_1_flags, FLAGS, F_V, F_N, F_Z, F_C}),
    .RVALUE(iomem_1_rvalue), .PORTA(PORTA), .PORTB(PORTB), .TTX(TTX), .PULSE(PULSE), .GIMSK(GIMSK),
    .GRAM_FLIP(iomem_1_gram_flip), .WRITER(iomem_1_writer), .READER(iomem_1_reader));
  assign xor_1_out = PINA_BUF_q ^ PINA;  // XOr xor_1, 16 bits wide
  zero zero_1 (.A(xor_1_out), .iszero(zero_1_iszero));
  Sub #(.Bits(16)) sub_1 (.a(multiplexer_9_out), .b(16'h69ff), .c_i(1'b0), .s(sub_1_s));  // open: c_o
  RAMDualPort #(.AddrBits(16), .Bits(16)) ramdualport_1 (
    .A(multiplexer_9_out), .Din(GPR_A), .str(and_15_out), .C(CLK_CPU), .ld(not_5_out), .D(ramdualport_1_d));
  Add #(.Bits(16)) add_3 (.a(iomem_1_sp), .b(multiplexer_11_out), .c_i(1'b0), .s(add_3_s));  // open: c_o
  GraphicCard #(.graphicHeight(120), .Bits(16)) graphiccard_1 (
    .A(sub_1_s), .str(and_17_out), .C(CLK_CPU), .ld(1'b0), .B(iomem_1_gram_flip[0]), .D(GPR_A));
  and and_17 (and_17_out, and_15_out, comparator_3_lt);
  Comparator #(.Bits(16)) comparator_3 (.a(16'h69ff), .b(multiplexer_9_out), .lt(comparator_3_lt));  // open: gt, eq
  Multiplexer #(.Bits(16)) multiplexer_11 (.sel(and_14_out), .in_0(16'h1), .in_1({16{1'b1}}), .out(multiplexer_11_out));
  not not_6 (not_6_out, zero_1_iszero);
  Multiplexer #(.Bits(16)) multiplexer_12 (
    .sel(comparator_2_lt), .in_0(ramdualport_1_d), .in_1(iomem_1_rvalue), .out(multiplexer_12_out));
  Multiplexer #(.Bits(16)) multiplexer_13 (
    .sel(and_18_out), .in_0(multiplexer_12_out), .in_1(IMM), .out(multiplexer_13_out));
  Comparator #(.Bits(3)) comparator_4 (.a(INSTR[11:9]), .b(3'b110), .eq(comparator_4_eq));  // open: gt, lt
  RS_FF rs_ff_1 (.S(not_6_out), .C(PHASE_2), .R(1'b0), .Q(INT_PINA));  // open: nQ
  or or_4 (or_4_out, ELPM_9__11, comparator_4_eq);
  and and_18 (and_18_out, MODE_MEM, or_4_out);
  Multiplexer #(.Bits(16)) multiplexer_14 (
    .sel(not_7_out), .in_0(iomem_1_writer), .in_1(iomem_1_reader), .out(multiplexer_14_out));
  Comparator #(.Bits(3)) comparator_5 (.a(INSTR[11:9]), .b(3'b111), .eq(ELPM_9__11));  // open: gt, lt
  not not_7 (not_7_out, INSTR[8]);

  // Other names for the same wires on the sheet: FLAGS[3:0] = {F_V, F_N, F_Z, F_C}; INSTR_8 = INSTR[8]

  // Notes on the sheet:
  //   CLK_CPU: Hz: 5
  //   contents of lookuptable_1 (hex, n*v repeats v):
  //   0,a,1
  //   contents of IS_STACK (hex, n*v repeats v):
  //   0,1
  //   contents of IS_RW (hex, n*v repeats v):
  //   5*0,1
  //   contents of ADDRBUS_SEL (hex, n*v repeats v):
  //   4*0,1,2
endmodule
