// Digital circuit ALU.dig as structural Verilog
module ALU (
  input  [15:0] A,
  input  [15:0] B,
  input  [4:0] OP,
  input  C_en,
  input  C_in,
  input  CS,
  output [15:0] R,
  output R_N,
  output R_C,
  output R_V,
  output R_Z
);

  wire and_3_out, and_4_out, and_5_out, and_6_out, and_7_out, driver_1_out, driver_4_out, not_2_out;
  wire [3:0] driver_3_out;
  wire [4:0] driver_5_out, lea_shwhich_out;
  wire [4:4] driver_3_out_2;
  wire [15:0] add_1_s, and_2_out, driver_2_out, idiv_q, idiv_r, inc_dec_s, lea_adder_s, lea_mul_out,
       lsh_rol_out, multiplexer_1_out, multiplexer_2_out, multiplexer_3_out, multiplexer_4_out,
       multiplexer_5_out, not_1_out, or_1_out, or_2_out, or_3_out, rsh_ror_out, sub_1_s, udiv_q, udiv_r,
       xor_1_out;
  wire [15:5] driver_5_out_2;
  wire [15:15] and_1_out;
  wire [31:0] imul_mul, umul_mul;

  assign driver_1_out = CS ? C_en : 1'bz;  // Driver driver_1
  assign driver_2_out = CS ? A : 16'bz;  // Driver driver_2
  assign {driver_3_out_2[4], driver_3_out} = CS ? OP : 5'bz;  // Driver driver_3
  PullDown pulldown_1 (.out(driver_1_out));
  assign driver_4_out = CS ? C_in : 1'bz;  // Driver driver_4
  PullDown #(.Bits(16)) pulldown_2 (.out(driver_2_out));
  assign {driver_5_out_2, driver_5_out} = CS ? B : 16'bz;  // Driver driver_5
  PullDown #(.Bits(5)) pulldown_3 (.out({driver_3_out_2[4], driver_3_out}));
  PullDown pulldown_4 (.out(driver_4_out));
  PullDown #(.Bits(16)) pulldown_5 (.out({driver_5_out_2, driver_5_out}));
  and and_1 (and_1_out[15], driver_1_out, driver_4_out);
  LookUpTable #(.Bits(5)) lea_shwhich (
    .in0(driver_3_out[0]), .in1(driver_3_out[1]), .in2(driver_3_out[2]), .in3(driver_3_out[3]),
    .out(lea_shwhich_out));
  Multiplexer #(.Bits(16)) multiplexer_1 (.sel(driver_1_out), .in_0(16'h1), .in_1({16{1'b1}}), .out(multiplexer_1_out));
  Add #(.Bits(16)) add_1 (
    .a(driver_2_out), .b({driver_5_out_2, driver_5_out}), .c_i(and_1_out[15]), .s(add_1_s));  // open: c_o
  Sub #(.Bits(16)) sub_1 (
    .a(driver_2_out), .b({driver_5_out_2, driver_5_out}), .c_i(and_1_out[15]), .s(sub_1_s));  // open: c_o
  BarrelShifter #(.Bits(16)) lsh_rol (.in(driver_2_out), .shift(driver_5_out), .out(lsh_rol_out));
  BarrelShifter #(.Bits(16), .direction("right")) rsh_ror (.in(driver_2_out), .shift(driver_5_out), .out(rsh_ror_out));
  assign not_1_out = ~driver_2_out;  // Not not_1, 16 bits wide
  assign or_1_out = driver_2_out | {driver_5_out_2, driver_5_out};  // Or or_1, 16 bits wide
  assign xor_1_out = driver_2_out ^ {driver_5_out_2, driver_5_out};  // XOr xor_1, 16 bits wide
  assign and_2_out = driver_2_out & {driver_5_out_2, driver_5_out};  // And and_2, 16 bits wide
  BarrelShifter #(.Bits(16)) lea_mul (.in({driver_5_out_2, driver_5_out}), .shift(lea_shwhich_out), .out(lea_mul_out));
  Div #(.Bits(16)) udiv (.a(driver_2_out), .b({driver_5_out_2, driver_5_out}), .q(udiv_q), .r(udiv_r));
  Div #(.Signed("true"), .Bits(16)) idiv (.a(driver_2_out), .b({driver_5_out_2, driver_5_out}), .q(idiv_q), .r(idiv_r));
  Add #(.Bits(16)) inc_dec (.a(driver_2_out), .b(multiplexer_1_out), .c_i(1'b0), .s(inc_dec_s));  // open: c_o
  Mul #(.Bits(16)) umul (.a(driver_2_out), .b({driver_5_out_2, driver_5_out}), .mul(umul_mul));
  Mul #(.Signed("true"), .Bits(16)) imul (.a(driver_2_out), .b({driver_5_out_2, driver_5_out}), .mul(imul_mul));
  Multiplexer #(.Bits(16)) multiplexer_2 (
    .sel(driver_3_out_2[4]), .in_0(udiv_q), .in_1(udiv_r), .out(multiplexer_2_out));
  Multiplexer #(.Bits(16)) multiplexer_3 (
    .sel(driver_3_out_2[4]), .in_0(idiv_q), .in_1(idiv_r), .out(multiplexer_3_out));
  Multiplexer #(.Bits(16)) multiplexer_4 (
    .sel(driver_1_out), .in_0(umul_mul[15:0]), .in_1(imul_mul[15:0]), .out(multiplexer_4_out));
  assign or_2_out = {{15{1'b0}}, and_1_out[15]} | lsh_rol_out;  // Or or_2, 16 bits wide
  Add #(.Bits(16)) lea_adder (.a(driver_2_out), .b(lea_mul_out), .c_i(1'b0), .s(lea_adder_s));  // open: c_o
  Multiplexer #(.Bits(16)) multiplexer_5 (
    .sel(driver_1_out), .in_0(multiplexer_2_out), .in_1(multiplexer_3_out), .out(multiplexer_5_out));
  assign or_3_out = {and_1_out[15], {15{1'b0}}} | rsh_ror_out;  // Or or_3, 16 bits wide
  Multiplexer #(.Selector_Bits(4), .Bits(16)) multiplexer_6 (
    .sel(driver_3_out), .in_0({driver_5_out_2, driver_5_out}), .in_1(add_1_s), .in_2(sub_1_s),
    .in_3(multiplexer_4_out), .in_4(or_2_out), .in_5(or_3_out), .in_6(not_1_out), .in_7(or_1_out),
    .in_8(xor_1_out), .in_9(and_2_out), .in_10(lea_adder_s), .in_11(lea_adder_s), .in_12(lea_adder_s),
    .in_13(multiplexer_5_out), .in_14(inc_dec_s), .in_15(sub_1_s), .out(R));
  and and_3 (and_3_out, driver_2_out[15], driver_5_out_2[15]);
  and and_4 (and_4_out, ~driver_2_out[15], ~driver_5_out_2[15], ~not_2_out);  // And
  and and_5 (and_5_out, not_2_out, driver_5_out_2[15], driver_2_out[15]);
  and and_6 (and_6_out, driver_2_out[15], not_2_out);
  and and_7 (and_7_out, driver_5_out_2[15], not_2_out);
  not not_2 (not_2_out, R[15]);
  or or_4 (R_V, and_4_out, and_5_out);
  or or_5 (R_C, and_6_out, and_3_out, and_7_out);
  Comparator #(.Bits(16)) comparator_1 (.a(R), .b({16{1'b0}}), .eq(R_Z));  // open: gt, lt

  assign R_N = R[15];

  // Notes on the sheet:
  //   contents of lea_shwhich (hex, n*v repeats v):
  //   10*0,1,2,3
endmodule
