// Digital circuit Demo1.dig as structural Verilog
module Demo1 (
  input  clk,
  output [15:0] PORTA_TEST
);

  wire [15:0] _2023cpu16_1_portb, _2023cpu16_1_rom_addr, _2023cpu16_1_rom_imm_addr, _2023cpu16_1_ttx,
       PROGFLASH_d1, PROGFLASH_d2;

  ROMDualPort #(.AddrBits(16), .isProgramMemory("true"), .Bits(16)) PROGFLASH (
    .A1(_2023cpu16_1_rom_addr), .s1(1'b1), .A2(_2023cpu16_1_rom_imm_addr), .s2(1'b1), .D1(PROGFLASH_d1),
    .D2(PROGFLASH_d2));
  _2023CPU16 _2023cpu16_1 (
    .ROM_INSTR(PROGFLASH_d1), .ROM_IMM(PROGFLASH_d2), .CLK_CPU(clk), .ROM_ADDR(_2023cpu16_1_rom_addr),
    .ROM_IMM_ADDR(_2023cpu16_1_rom_imm_addr), .PORTA(PORTA_TEST), .PORTB(_2023cpu16_1_portb),
    .TTX(_2023cpu16_1_ttx));  // open: PINA, PINB, TRX, PULSE

  // Notes on the sheet:
  //   clk: Hz: 2147483647
  //   PROGFLASH loads Fib.bin
endmodule
