// Digital circuit rand.dig as structural Verilog
module \rand  (
  input  CLK_RAND,
  output [15:0] RAND
);

  wire [15:0] notconnected_1_out;

  // NotConnected on notconnected_1_out
  D_FF #(.Bits(16)) d_ff_1 (.D(notconnected_1_out), .C(CLK_RAND), .Q(RAND));  // open: nQ

  // Notes on the sheet:
  //   CLK_RAND: Hz: 10
endmodule
