// Digital circuit tetris.dig as structural Verilog
module tetris (
  input  clk
);

  wire [0:0] keyboard_1_av;
  wire [15:0] _2023cpu16_1_porta, _2023cpu16_1_portb, _2023cpu16_1_pulse, _2023cpu16_1_rom_addr,
       _2023cpu16_1_rom_imm_addr, _2023cpu16_1_ttx, keyboard_1_d, PROGFLASH_d1, PROGFLASH_d2;

  ROMDualPort #(.AddrBits(16), .isProgramMemory("true"), .Bits(16)) PROGFLASH (
    .A1(_2023cpu16_1_rom_addr), .s1(1'b1), .A2(_2023cpu16_1_rom_imm_addr), .s2(1'b1), .D1(PROGFLASH_d1),
    .D2(PROGFLASH_d2));
  Keyboard keyboard_1 (.C(_2023cpu16_1_pulse[0]), .en(1'b1), .D(keyboard_1_d), .av(keyboard_1_av[0]));
  _2023CPU16 _2023cpu16_1 (
    .ROM_INSTR(PROGFLASH_d1), .ROM_IMM(PROGFLASH_d2), .CLK_CPU(clk), .PINA({{15{1'b0}}, keyboard_1_av[0]}),
    .TRX(keyboard_1_d), .ROM_ADDR(_2023cpu16_1_rom_addr), .ROM_IMM_ADDR(_2023cpu16_1_rom_imm_addr),
    .PORTA(_2023cpu16_1_porta), .PORTB(_2023cpu16_1_portb), .TTX(_2023cpu16_1_ttx), .PULSE(_2023cpu16_1_pulse));  // open: PINB
  Terminal terminal_1 (.D(_2023cpu16_1_ttx), .C(_2023cpu16_1_pulse[0]), .en(_2023cpu16_1_pulse[0]));

  // Notes on the sheet:
  //   clk: Hz: 2147483647
  //   PROGFLASH loads tetris.bin
endmodule
