// Digital circuit timercounter.dig as structural Verilog
module timercounter (
  input  CLK_KHz,
  output [15:0] TCNT,
  output OVF
);

  Counter #(.Bits(16)) counter_1 (.en(1'b1), .C(CLK_KHz), .clr(OVF), .out(TCNT), .ovf(OVF));

  // Notes on the sheet:
  //   CLK_KHz: Hz: 1000
endmodule
